# Fritzing sketch display_i2c (saved by Fritzing 0.7.11b)
breadboards: 1

parts:
  Arduino1 = Arduino
  7_Segment1 = 7 Segment Display  # not connected
  7_Segment2 = 7 Segment Display  # not connected
  7_Segment3 = 7 Segment Display  # not connected
  7_Segment4 = 7 Segment Display  # not connected
  R1 = 4.7k Ω Resistor [package=THT]
  R2 = 4.7k Ω Resistor [package=THT]

nets:
  N1: Arduino1.+5V, R1.Pin_1, R2.Pin_1
  N2: Arduino1.A4, R1.Pin_0
  N3: Arduino1.A5, R2.Pin_0
