# Fritzing sketch thermistor (saved by Fritzing 0.7.11b)
breadboards: 1

parts:
  Arduino1 = Arduino
  R1 = Temperature Sensor (Thermistor) [thermistor_type=NTC package=THT]
  R2 = 10k Ω Resistor [package=THT]

nets:
  N1: Arduino1.+5V, R1.pin_0
  N2: Arduino1.GND, R2.Pin_1
  N3: Arduino1.A0, R1.pin_1, R2.Pin_0
