# Fritzing sketch thermometer (saved by Fritzing 0.7.11b)
breadboards: 1

parts:
  Arduino1 = Arduino
  R3 = 4.7k Ω Resistor [package=THT]
  R4 = 4.7k Ω Resistor [package=THT]
  R5 = 10k Ω Resistor [package=THT]
  R7 = Temperature Sensor (Thermistor) [package=THT]
  7_Segment1 = 7 Segment Display
  7_Segment2 = 7 Segment Display  # not connected
  7_Segment3 = 7 Segment Display  # not connected
  7_Segment4 = 7 Segment Display  # not connected

nets:
  N1: Arduino1.+5V, R3.Pin_0, R4.Pin_0, R7.pin_0
  N2: Arduino1.GND, R5.Pin_1
  N3: Arduino1.A0, R5.Pin_0, R7.pin_1
  N4: Arduino1.A4, R4.Pin_1
  N5: Arduino1.A5, R3.Pin_1
  N6: 7_Segment1.Segment_C, 7_Segment1.Segment_A
  N7: 7_Segment1.Segment_DP, 7_Segment1.Segment_B
